# Fritzing sketch nodemcuv1_syhs220 (saved by Fritzing 0.9.3b)
breadboards: 1

parts:
  U1 = NodeMCU V1.0
  Part1 = Humidity Sensor - HIH-4030 Breakout
  V1 = DC Power [voltage=5]  # not connected

nets:
  GND: U1.GND, Part1.GND
  N1: U1.A0, Part1.OUT

notes:
  +5V
  GND

custom parts:
  NodeMCU V1.0: ESP8266 based NodeMCU
